# Fritzing sketch circutDesign (saved by Fritzing 0.9.3b)

parts:
  Raspberry_Pi_Zero1 = Raspberry Pi Zero
  U1 = WS2812 RGB LED strip
  RESET = Pushbutton [package="[THT]"]
  J1 = screw terminal, 4 pins
  J2 = Screw terminal - 2 pins [package=THT]

nets:
  N1: Raspberry_Pi_Zero1.GND, Raspberry_Pi_Zero1.GPIO18, RESET.Pin_3, RESET.Pin_4, J2.pin1, J2.pin2
  N2: U1.GND, J1.pin2
  N3: U1.VCC, J1.pin3
  N4: U1.DIN, J1.pin1

custom parts:
  WS2812 RGB LED strip: WS2812 strip
